// Logisim project processor.circ as structural Verilog: 6 circuits, main circuit main
module main (
  input  in_1,
  input  [2:0] in_2,
  input  [2:0] in_3,
  input  [31:0] Instruction,
  output [31:0] out_5,
  output [31:0] out_6
);

  RegisterFile registerfile_1 (.CLK(in_1), .A1(in_2), .A2(in_3), .RD1(out_5), .RD2(out_6));  // open: WD3, WE3, A3, v0
  ControlUnit controlunit_1 (.Instruction(Instruction));  // open: RegDst, RegWrite, ALUControl, Branch, ALUSrc, MemWrite
  ALU alu_1 ();  // open: F, B, A, out_6, in_3, out_5
endmodule

module ALU (
  input  [2:0] F,
  input  [31:0] B,
  input  [31:0] in_3,
  input  [31:0] A,
  output out_5,
  output [31:0] out_6
);

  wire [30:0] adder_1_out;
  wire [31:0] and_1_out, bit_extender_1_out, multiplexer_1_out, not_1_out, or_1_out;
  wire [31:31] adder_1_out_2;

  assign not_1_out = ~B;  // NOT_Gate not_1, 32 bits wide
  Multiplexer #(.width(32), .enable("false")) multiplexer_1 (
    .in0(B), .in1(not_1_out), .out(multiplexer_1_out), .sel(F[2]));
  Adder #(.width(32)) adder_1 (
    .a(multiplexer_1_out), .b(A), .out({adder_1_out_2[31], adder_1_out}), .cin(F[2]));  // open: cout
  assign and_1_out = multiplexer_1_out & A;  // AND_Gate and_1, 32 bits wide
  assign or_1_out = multiplexer_1_out | A;  // OR_Gate or_1, 32 bits wide
  assign bit_extender_1_out = {{31{1'b0}}, adder_1_out_2[31]};  // Bit_Extender bit_extender_1
  Multiplexer #(.select(2), .width(32), .enable("false")) multiplexer_2 (
    .in0(and_1_out), .in1(or_1_out), .in2({adder_1_out_2[31], adder_1_out}), .in3(bit_extender_1_out),
    .out(out_6), .sel(F[1:0]));
  Comparator #(.width(32), .mode("unsigned")) comparator_1 (.a(out_6), .b(in_3), .eq(out_5));  // open: gt, lt
endmodule

module Datapath (
  output [31:0] v0
);

  wire clock_1_out;
  wire [7:0] register_1_q, shifter_1_out, undriven;

  Clock clock_1 (.out(clock_1_out));
  Register register_1 (.D(undriven), .Q(register_1_q), .clk(clock_1_out));  // open: en, clr
  Shifter #(.shift("lr")) shifter_1 (.in(register_1_q), .\dist (3'b010), .out(shifter_1_out));
  ROM #(.dataWidth(32)) rom_1 (.addr(shifter_1_out));  // open: data, sel
  ControlUnit controlunit_1 ();  // open: Instruction, RegDst, RegWrite, ALUControl, Branch, ALUSrc, MemWrite

  // Notes on the sheet:
  //   contents of rom_1 (hex, n*v repeats v):
  //   aa bbbbbbbb cc
endmodule

module Tests (
  output [31:0] Y,
  output [7:0] out_2,
  output [7:0] out_3,
  output [2:0] out_4
);

  BitSelector #(.width(32), .group(8)) bitselector_1 (.in(32'h12356789), .out(out_2), .sel(2'b01));
  BitSelector #(.width(32), .group(8)) bitselector_2 (.in(32'h12356789), .out(out_3), .sel(2'b01));
  BitSelector #(.group(3)) bitselector_3 (.in(out_3), .out(out_4), .sel(2'b00));

  assign Y = 32'hf4010207;

  // Notes on the sheet:
  //   binary values in Logisim. Convince yourself how the bits are displayed.
  //   Example 2: The bit selector is configured to have 32  
  //   bit group #1 (starting at index 0) is selected for the output.
  //   That is, the 8 bits 0x67 at bit indices 15..8  are sent to the output.
  //   Example 3: Now, assume that you want to extract 3 bits at   
  //   Example 1: A simple example that illustrates how 32-bit values are displayed as 
  //   input bits and 8 output bits. The parameter constant is 1, which means that   
  //   bit indices 10..8. This can be accoplished by putting two bit selecotrs in series.
endmodule

module RegisterFile (
  input  CLK,
  input  [2:0] A1,
  input  [31:0] WD3,
  input  [2:0] A2,
  input  WE3,
  input  [2:0] A3,
  output [31:0] RD1,
  output [31:0] RD2,
  output [31:0] v0
);

  wire and_1_out, and_2_out, and_3_out, and_4_out, and_5_out, and_6_out, and_7_out, decoder_1_out0,
       decoder_1_out1, decoder_1_out2, decoder_1_out3, decoder_1_out4, decoder_1_out5, decoder_1_out6,
       decoder_1_out7;
  wire [31:0] a0_q, a1_q, a2_q, a3_q, at_q, bit_extender_1_out, v1_q;

  Decoder #(.select(3)) decoder_1 (
    .out0(decoder_1_out0), .out1(decoder_1_out1), .out2(decoder_1_out2), .out3(decoder_1_out3),
    .out4(decoder_1_out4), .out5(decoder_1_out5), .out6(decoder_1_out6), .out7(decoder_1_out7), .sel(A3));  // open: en
  and and_1 (and_1_out, WE3, decoder_1_out1);
  and and_2 (and_2_out, WE3, decoder_1_out2);
  and and_3 (and_3_out, WE3, decoder_1_out3);
  and and_4 (and_4_out, WE3, decoder_1_out4);
  and and_5 (and_5_out, WE3, decoder_1_out5);
  and and_6 (and_6_out, WE3, decoder_1_out6);
  and and_7 (and_7_out, WE3, decoder_1_out7);
  assign bit_extender_1_out = {{31{1'b0}}, decoder_1_out0};  // Bit_Extender bit_extender_1
  Register #(.width(32)) at (.D(WD3), .en(and_1_out), .Q(at_q), .clk(CLK));  // open: clr
  Register #(.width(32)) u_v0 (.D(WD3), .en(and_2_out), .Q(v0), .clk(CLK));  // open: clr
  Register #(.width(32)) v1 (.D(WD3), .en(and_3_out), .Q(v1_q), .clk(CLK));  // open: clr
  Register #(.width(32)) a0 (.D(WD3), .en(and_4_out), .Q(a0_q), .clk(CLK));  // open: clr
  Register #(.width(32)) u_a1 (.D(WD3), .en(and_5_out), .Q(a1_q), .clk(CLK));  // open: clr
  Register #(.width(32)) u_a2 (.D(WD3), .en(and_6_out), .Q(a2_q), .clk(CLK));  // open: clr
  Register #(.width(32)) u_a3 (.D(WD3), .en(and_7_out), .Q(a3_q), .clk(CLK));  // open: clr
  Multiplexer #(.select(3), .width(32)) multiplexer_1 (
    .in0(bit_extender_1_out), .in1(at_q), .in2(v0), .in3(v1_q), .in4(a0_q), .in5(a1_q), .in6(a2_q),
    .in7(a3_q), .out(RD1), .sel(A1));  // open: en
  Multiplexer #(.select(3), .width(32)) multiplexer_2 (
    .in0(bit_extender_1_out), .in1(at_q), .in2(v0), .in3(v1_q), .in4(a0_q), .in5(a1_q), .in6(a2_q),
    .in7(a3_q), .out(RD2), .sel(A2));  // open: en

  // Notes on the sheet:
  //   $0
endmodule

module ControlUnit (
  input  [31:0] Instruction,
  output RegDst,
  output RegWrite,
  output ALUSrc,
  output [2:0] ALUControl,
  output Branch,
  output MemWrite
);

  wire [5:0] bitselector_1_out;
  wire [31:0] shifter_1_out;

  Shifter #(.width(32), .shift("lr")) shifter_1 (.in(Instruction), .\dist (5'b11010), .out(shifter_1_out));
  BitSelector #(.width(32), .group(6)) bitselector_1 (.in(shifter_1_out), .out(bitselector_1_out), .sel(3'b000));
  Comparator #(.width(6), .mode("unsigned")) comparator_1 (
    .a(bitselector_1_out), .b(6'b001000), .eq(ALUSrc));  // open: gt, lt
  Comparator #(.width(6), .mode("unsigned")) comparator_2 (
    .a(bitselector_1_out), .b({6{1'b0}}), .eq(RegDst));  // open: gt, lt
  Comparator #(.width(6), .mode("unsigned")) comparator_3 (
    .a(bitselector_1_out), .b(6'b000100), .eq(Branch));  // open: gt, lt
  Comparator #(.width(6), .mode("unsigned")) comparator_4 (
    .a(bitselector_1_out), .b(6'b010011), .eq(MemWrite));  // open: gt, lt
  or or_1 (RegWrite, ALUSrc, RegDst);

  assign ALUControl = 3'b010;

  // Notes on the sheet:
  //   op
endmodule
